// Logisim project Trabalho.circ as structural Verilog: 17 circuits, main circuit main
module main (
);


  // Notes on the sheet:
  //   e depois use aquele circuito para construir sua calculadora.
  //   Este projeto foi fornecido apenas para que você altere o circuito alu-8-bits,
endmodule

module alu_8_bits (
  input  [7:0] A,
  input  [7:0] B,
  input  [2:0] OP,
  input  Cin,
  output [7:0] s,
  output c,
  output z
);

  DMUX_1_8_8bit dmux_1_8_8bit_1 (.MUX(OP), .A(A));  // open: S8, S7, S6, S5, S4, S3, S2, S1
  DMUX_1_8_8bit dmux_1_8_8bit_2 (.MUX(OP), .A(B));  // open: S8, S7, S6, S5, S4, S3, S2, S1
endmodule

module somador_2_bits (
  input  A,
  input  B,
  input  Qin,
  output S,
  output Qout
);

  wire and_1_out, and_2_out, and_3_out, and_4_out, and_5_out, and_6_out, and_7_out, not_1_out, not_2_out,
       not_3_out, not_4_out, not_5_out, not_6_out;

  not not_1 (not_1_out, A);
  not not_2 (not_2_out, B);
  not not_3 (not_3_out, A);
  not not_4 (not_4_out, Qin);
  not not_5 (not_5_out, B);
  not not_6 (not_6_out, Qin);
  and and_1 (and_1_out, B, Qin);
  and and_2 (and_2_out, A, Qin);
  and and_3 (and_3_out, A, B);
  and and_4 (and_4_out, not_1_out, not_2_out, Qin);
  and and_5 (and_5_out, not_3_out, B, not_4_out);
  and and_6 (and_6_out, A, not_5_out, not_6_out);
  and and_7 (and_7_out, A, B, Qin);
  or or_1 (Qout, and_1_out, and_2_out, and_3_out);
  or or_2 (S, and_4_out, and_5_out, and_6_out, and_7_out);
endmodule

module somador_8_bits (
  input  [7:0] A,
  input  [7:0] B,
  output [7:0] S,
  output Qout
);

  wire somador_2_bits_2_qout, somador_2_bits_3_qout, somador_2_bits_4_qout, somador_2_bits_5_qout,
       somador_2_bits_6_qout, somador_2_bits_7_qout, somador_2_bits_8_qout;

  somador_2_bits somador_2_bits_1 (.A(A[7]), .B(B[7]), .Qin(somador_2_bits_2_qout), .S(S[7]), .Qout(Qout));
  somador_2_bits somador_2_bits_2 (
    .A(A[6]), .B(B[6]), .Qin(somador_2_bits_3_qout), .S(S[6]), .Qout(somador_2_bits_2_qout));
  somador_2_bits somador_2_bits_3 (
    .A(A[5]), .B(B[5]), .Qin(somador_2_bits_4_qout), .S(S[5]), .Qout(somador_2_bits_3_qout));
  somador_2_bits somador_2_bits_4 (
    .A(A[4]), .B(B[4]), .Qin(somador_2_bits_5_qout), .S(S[4]), .Qout(somador_2_bits_4_qout));
  somador_2_bits somador_2_bits_5 (
    .A(A[3]), .B(B[3]), .Qin(somador_2_bits_6_qout), .S(S[3]), .Qout(somador_2_bits_5_qout));
  somador_2_bits somador_2_bits_6 (
    .A(A[2]), .B(B[2]), .Qin(somador_2_bits_7_qout), .S(S[2]), .Qout(somador_2_bits_6_qout));
  somador_2_bits somador_2_bits_7 (
    .A(A[1]), .B(B[1]), .Qin(somador_2_bits_8_qout), .S(S[1]), .Qout(somador_2_bits_7_qout));
  somador_2_bits somador_2_bits_8 (.A(A[0]), .B(B[0]), .Qin(1'b0), .S(S[0]), .Qout(somador_2_bits_8_qout));
endmodule

module XOR_2_bits (
  input  A,
  input  B,
  output S
);

  wire and_1_out, and_2_out, not_1_out, not_2_out;

  not not_1 (not_1_out, A);
  not not_2 (not_2_out, B);
  and and_1 (and_1_out, not_1_out, B);
  and and_2 (and_2_out, A, not_2_out);
  or or_1 (S, and_1_out, and_2_out);
endmodule

module XOR_8_bits (
  input  [7:0] A,
  input  [7:0] B,
  output [7:0] S
);

  XOR_2_bits xor_2_bits_1 (.A(A[7]), .B(B[7]), .S(S[7]));
  XOR_2_bits xor_2_bits_2 (.A(A[6]), .B(B[6]), .S(S[6]));
  XOR_2_bits xor_2_bits_3 (.A(A[5]), .B(B[5]), .S(S[5]));
  XOR_2_bits xor_2_bits_4 (.A(A[4]), .B(B[4]), .S(S[4]));
  XOR_2_bits xor_2_bits_5 (.A(A[3]), .B(B[3]), .S(S[3]));
  XOR_2_bits xor_2_bits_6 (.A(A[2]), .B(B[2]), .S(S[2]));
  XOR_2_bits xor_2_bits_7 (.A(A[1]), .B(B[1]), .S(S[1]));
  XOR_2_bits xor_2_bits_8 (.A(A[0]), .B(B[0]), .S(S[0]));
endmodule

module AND_8_bits (
  input  [7:0] A,
  input  [7:0] B,
  output [7:0] S
);

  and and_1 (S[7], A[7], B[7]);
  and and_2 (S[6], A[6], B[6]);
  and and_3 (S[5], A[5], B[5]);
  and and_4 (S[4], A[4], B[4]);
  and and_5 (S[3], A[3], B[3]);
  and and_6 (S[2], A[2], B[2]);
  and and_7 (S[1], A[1], B[1]);
  and and_8 (S[0], A[0], B[0]);
endmodule

module OR_8_bits (
  input  [7:0] A,
  input  [7:0] B,
  output [7:0] S
);

  or or_1 (S[7], A[7], B[7]);
  or or_2 (S[6], A[6], B[6]);
  or or_3 (S[5], A[5], B[5]);
  or or_4 (S[3], A[3], B[3]);
  or or_5 (S[4], A[4], B[4]);
  or or_6 (S[2], A[2], B[2]);
  or or_7 (S[1], A[1], B[1]);
  or or_8 (S[0], A[0], B[0]);
endmodule

module Shift_Left_8_bits (
  input  [7:0] B,
  output [7:0] S
);


  assign S = {B[6:0], 1'b0};
endmodule

module Shift_Right_8_bits (
  input  [7:0] B,
  output [7:0] S
);


  assign S = {1'b0, B[7:1]};
endmodule

module Mux_2_1_1_bit (
  input  A,
  input  B,
  input  Mux,
  output S
);

  wire and_1_out, and_2_out, not_1_out;

  not not_1 (not_1_out, Mux);
  and and_1 (and_1_out, B, Mux);
  and and_2 (and_2_out, A, not_1_out);
  or or_1 (S, and_1_out, and_2_out);
endmodule

module Mux_2_1_8_bits (
  input  MUX,
  input  [7:0] A,
  input  [7:0] B,
  output [7:0] S
);

  Mux_2_1_1_bit mux_2_1_1_bit_1 (.A(B[7]), .B(MUX), .Mux(A[7]), .S(S[7]));
  Mux_2_1_1_bit mux_2_1_1_bit_2 (.A(B[6]), .B(MUX), .Mux(A[6]), .S(S[6]));
  Mux_2_1_1_bit mux_2_1_1_bit_3 (.A(B[5]), .B(MUX), .Mux(A[5]), .S(S[5]));
  Mux_2_1_1_bit mux_2_1_1_bit_4 (.A(B[4]), .B(MUX), .Mux(A[4]), .S(S[4]));
  Mux_2_1_1_bit mux_2_1_1_bit_5 (.A(B[3]), .B(MUX), .Mux(A[3]), .S(S[3]));
  Mux_2_1_1_bit mux_2_1_1_bit_6 (.A(B[2]), .B(MUX), .Mux(A[2]), .S(S[2]));
  Mux_2_1_1_bit mux_2_1_1_bit_7 (.A(B[0]), .B(MUX), .Mux(A[0]), .S(S[0]));
  Mux_2_1_1_bit mux_2_1_1_bit_8 (.A(B[1]), .B(MUX), .Mux(A[1]), .S(S[1]));
endmodule

module Mux_4_1_8_bits (
  input  [7:0] A,
  input  [7:0] B,
  output [7:0] out_3
);

  Mux_2_1_8_bits mux_2_1_8_bits_1 (.A(A), .B(B));  // open: S, MUX
endmodule

module SUB (
  input  [7:0] A,
  input  [7:0] B,
  output [7:0] S,
  output Qout
);

  wire not_2_out, not_3_out, not_4_out, not_5_out, not_6_out, not_7_out, not_8_out, not_9_out,
       somador_2_bits_1_qout, somador_2_bits_2_qout, somador_2_bits_3_qout, somador_2_bits_4_qout,
       somador_2_bits_5_qout, somador_2_bits_6_qout, somador_2_bits_7_qout, somador_2_bits_8_qout;

  not not_1 (Qout, somador_2_bits_1_qout);
  not not_2 (not_2_out, B[7]);
  not not_3 (not_3_out, B[6]);
  not not_4 (not_4_out, B[5]);
  not not_5 (not_5_out, B[4]);
  not not_6 (not_6_out, B[3]);
  not not_7 (not_7_out, B[2]);
  not not_8 (not_8_out, B[1]);
  not not_9 (not_9_out, B[0]);
  somador_2_bits somador_2_bits_1 (
    .A(A[7]), .B(not_2_out), .Qin(somador_2_bits_2_qout), .S(S[7]), .Qout(somador_2_bits_1_qout));
  somador_2_bits somador_2_bits_2 (
    .A(A[6]), .B(not_3_out), .Qin(somador_2_bits_3_qout), .S(S[6]), .Qout(somador_2_bits_2_qout));
  somador_2_bits somador_2_bits_3 (
    .A(A[5]), .B(not_4_out), .Qin(somador_2_bits_4_qout), .S(S[5]), .Qout(somador_2_bits_3_qout));
  somador_2_bits somador_2_bits_4 (
    .A(A[4]), .B(not_5_out), .Qin(somador_2_bits_5_qout), .S(S[4]), .Qout(somador_2_bits_4_qout));
  somador_2_bits somador_2_bits_5 (
    .A(A[3]), .B(not_6_out), .Qin(somador_2_bits_6_qout), .S(S[3]), .Qout(somador_2_bits_5_qout));
  somador_2_bits somador_2_bits_6 (
    .A(A[2]), .B(not_7_out), .Qin(somador_2_bits_7_qout), .S(S[2]), .Qout(somador_2_bits_6_qout));
  somador_2_bits somador_2_bits_7 (
    .A(A[1]), .B(not_8_out), .Qin(somador_2_bits_8_qout), .S(S[1]), .Qout(somador_2_bits_7_qout));
  somador_2_bits somador_2_bits_8 (.A(A[0]), .B(not_9_out), .Qin(1'b1), .S(S[0]), .Qout(somador_2_bits_8_qout));
endmodule

module DMUX_1_2_1bit (
  input  A,
  input  Op,
  output S1,
  output S2
);

  wire not_1_out;

  not not_1 (not_1_out, Op);
  and and_1 (S2, A, Op);
  and and_2 (S1, A, not_1_out);
endmodule

module DMUX_1_2_8bit (
  input  MUX,
  input  [7:0] A,
  output [7:0] S1,
  output [7:0] S2
);

  DMUX_1_2_1bit dmux_1_2_1bit_1 (.A(A[7]), .Op(MUX), .S1(S1[7]), .S2(S2[7]));
  DMUX_1_2_1bit dmux_1_2_1bit_2 (.A(A[6]), .Op(MUX), .S1(S1[6]), .S2(S2[6]));
  DMUX_1_2_1bit dmux_1_2_1bit_3 (.A(A[5]), .Op(MUX), .S1(S1[5]), .S2(S2[5]));
  DMUX_1_2_1bit dmux_1_2_1bit_4 (.A(A[4]), .Op(MUX), .S1(S1[4]), .S2(S2[4]));
  DMUX_1_2_1bit dmux_1_2_1bit_5 (.A(A[3]), .Op(MUX), .S1(S1[3]), .S2(S2[3]));
  DMUX_1_2_1bit dmux_1_2_1bit_6 (.A(A[2]), .Op(MUX), .S1(S1[2]), .S2(S2[2]));
  DMUX_1_2_1bit dmux_1_2_1bit_7 (.A(A[1]), .Op(MUX), .S1(S1[1]), .S2(S2[1]));
  DMUX_1_2_1bit dmux_1_2_1bit_8 (.A(A[0]), .Op(MUX), .S1(S1[0]), .S2(S2[0]));
endmodule

module DMUX_1_8_8bit (
  input  [2:0] MUX,
  input  [7:0] A,
  output [7:0] S8,
  output [7:0] S6,
  output [7:0] S4,
  output [7:0] S2,
  output [7:0] S7,
  output [7:0] S5,
  output [7:0] S3,
  output [7:0] S1
);

  wire [7:0] dmux_1_2_8bit_3_s1, dmux_1_2_8bit_3_s2, dmux_1_2_8bit_4_s1, dmux_1_2_8bit_4_s2,
       dmux_1_2_8bit_7_s1, dmux_1_2_8bit_7_s2;

  DMUX_1_2_8bit dmux_1_2_8bit_1 (.S1(S5), .MUX(MUX[0]), .S2(S6), .A(dmux_1_2_8bit_3_s1));
  DMUX_1_2_8bit dmux_1_2_8bit_2 (.S1(S7), .MUX(MUX[0]), .S2(S8), .A(dmux_1_2_8bit_3_s2));
  DMUX_1_2_8bit dmux_1_2_8bit_3 (
    .S1(dmux_1_2_8bit_3_s1), .MUX(MUX[1]), .S2(dmux_1_2_8bit_3_s2), .A(dmux_1_2_8bit_4_s2));
  DMUX_1_2_8bit dmux_1_2_8bit_4 (.S1(dmux_1_2_8bit_4_s1), .MUX(MUX[2]), .S2(dmux_1_2_8bit_4_s2), .A(A));
  DMUX_1_2_8bit dmux_1_2_8bit_5 (.S1(S3), .MUX(MUX[0]), .S2(S4), .A(dmux_1_2_8bit_7_s2));
  DMUX_1_2_8bit dmux_1_2_8bit_6 (.S1(S1), .MUX(MUX[0]), .S2(S2), .A(dmux_1_2_8bit_7_s1));
  DMUX_1_2_8bit dmux_1_2_8bit_7 (
    .S1(dmux_1_2_8bit_7_s1), .MUX(MUX[1]), .S2(dmux_1_2_8bit_7_s2), .A(dmux_1_2_8bit_4_s1));
endmodule
