// Logisim project renan_trabalho.circ as structural Verilog
module ADD (
  input  a,
  input  b,
  input  cin,
  output cout,
  output s
);

  wire and_1_out, and_2_out, and_3_out, and_4_out, and_5_out, and_6_out, and_7_out, not_1_out, not_2_out,
       not_3_out, not_4_out, not_5_out, not_6_out;

  and and_1 (and_1_out, b, cin);
  and and_2 (and_2_out, a, cin);
  and and_3 (and_3_out, a, b);
  not not_1 (not_1_out, a);
  not not_2 (not_2_out, b);
  not not_3 (not_3_out, a);
  not not_4 (not_4_out, cin);
  not not_5 (not_5_out, b);
  not not_6 (not_6_out, cin);
  or or_1 (cout, and_1_out, and_2_out, and_3_out);
  and and_4 (and_4_out, not_1_out, not_2_out, cin);
  and and_5 (and_5_out, not_3_out, b, not_4_out);
  and and_6 (and_6_out, a, not_5_out, not_6_out);
  and and_7 (and_7_out, a, b, cin);
  or or_2 (s, and_4_out, and_5_out, and_6_out, and_7_out);
endmodule

module ADD_8 (
  input  [7:0] in_1,
  input  [7:0] in_2,
  input  in_3,
  output [7:0] out_4
);

  wire add_1_cout, add_2_cout, add_3_cout, add_4_cout, add_5_cout, add_6_cout, add_7_cout;

  ADD add_1 (.a(in_2[0]), .b(in_1[0]), .cin(1'b0), .cout(add_1_cout), .s(out_4[0]));
  ADD add_2 (.a(in_2[1]), .b(in_1[1]), .cin(add_1_cout), .cout(add_2_cout), .s(out_4[1]));
  ADD add_3 (.a(in_2[2]), .b(in_1[2]), .cin(add_2_cout), .cout(add_3_cout), .s(out_4[2]));
  ADD add_4 (.a(in_2[3]), .b(in_1[3]), .cin(add_3_cout), .cout(add_4_cout), .s(out_4[3]));
  ADD add_5 (.a(in_2[4]), .b(in_1[4]), .cin(add_4_cout), .cout(add_5_cout), .s(out_4[4]));
  ADD add_6 (.a(in_2[5]), .b(in_1[5]), .cin(add_5_cout), .cout(add_6_cout), .s(out_4[5]));
  ADD add_7 (.a(in_2[6]), .b(in_1[6]), .cin(add_6_cout), .cout(add_7_cout), .s(out_4[6]));
  ADD add_8 (.a(in_2[7]), .b(in_1[7]), .cin(add_7_cout), .cout(in_3), .s(out_4[7]));
endmodule

module XOR (
  input  a,
  input  b,
  output s
);

  wire and_1_out, and_2_out, not_1_out, not_2_out;

  not not_1 (not_1_out, a);
  not not_2 (not_2_out, b);
  and and_1 (and_1_out, not_1_out, b);
  and and_2 (and_2_out, a, not_2_out);
  or or_1 (s, and_1_out, and_2_out);
endmodule

module XOR_8 (
  input  [7:0] in_1,
  input  [7:0] in_2,
  output [7:0] out_3
);

  XOR xor_1 (.a(in_2[0]), .b(in_1[0]), .s(out_3[0]));
  XOR xor_2 (.a(in_2[1]), .b(in_1[1]), .s(out_3[1]));
  XOR xor_3 (.a(in_2[2]), .b(in_1[2]), .s(out_3[2]));
  XOR xor_4 (.a(in_2[3]), .b(in_1[3]), .s(out_3[3]));
  XOR xor_5 (.a(in_2[4]), .b(in_1[4]), .s(out_3[4]));
  XOR xor_6 (.a(in_2[5]), .b(in_1[5]), .s(out_3[5]));
  XOR xor_7 (.a(in_2[6]), .b(in_1[6]), .s(out_3[6]));
  XOR xor_8 (.a(in_2[7]), .b(in_1[7]), .s(out_3[7]));
endmodule

module OR (
  input  a,
  input  b,
  output s
);

  or or_1 (s, b, a);
endmodule

module OR_8 (
  input  [7:0] in_1,
  input  [7:0] in_2,
  output [7:0] out_3
);

  OR or_1 (.a(in_2[0]), .b(in_1[0]), .s(out_3[0]));
  OR or_2 (.a(in_2[1]), .b(in_1[1]), .s(out_3[1]));
  OR or_3 (.a(in_2[2]), .b(in_1[2]), .s(out_3[2]));
  OR or_4 (.a(in_2[3]), .b(in_1[3]), .s(out_3[3]));
  OR or_5 (.a(in_2[4]), .b(in_1[4]), .s(out_3[4]));
  OR or_6 (.a(in_2[5]), .b(in_1[5]), .s(out_3[5]));
  OR or_7 (.a(in_2[6]), .b(in_1[6]), .s(out_3[6]));
  OR or_8 (.a(in_2[7]), .b(in_1[7]), .s(out_3[7]));
endmodule

module AND (
  input  a,
  input  b,
  output s
);

  and and_1 (s, a, b);
endmodule

module AND_8 (
  input  [7:0] in_1,
  input  [7:0] in_2,
  output [7:0] out_3
);

  AND and_1 (.a(in_2[0]), .b(in_1[0]), .s(out_3[0]));
  AND and_2 (.a(in_2[1]), .b(in_1[1]), .s(out_3[1]));
  AND and_3 (.a(in_2[2]), .b(in_1[2]), .s(out_3[2]));
  AND and_4 (.a(in_2[3]), .b(in_1[3]), .s(out_3[3]));
  AND and_5 (.a(in_2[4]), .b(in_1[4]), .s(out_3[4]));
  AND and_6 (.a(in_2[5]), .b(in_1[5]), .s(out_3[5]));
  AND and_7 (.a(in_2[6]), .b(in_1[6]), .s(out_3[6]));
  AND and_8 (.a(in_2[7]), .b(in_1[7]), .s(out_3[7]));
endmodule
